// Logisim project 1-OPEN THIS.circ as structural Verilog: 1 circuit, main circuit main
module main (
  input  A0,
  input  A1,
  input  A2,
  input  A3,
  input  B0,
  input  B1,
  input  B2,
  input  B3,
  input  S0,
  input  S1
);

  wire alu_1_p11, alu_1_p12, alu_1_p13, alu_1_p14, alu_1_p15, alu_1_p16, alu_1_p17, main_1_t0, main_1_u0,
       main_1_u1, main_1_u2, main_1_u3, n7448_1_p7, n7448_2_p7, n7448_2_p8, n7448_2_p9, n7448_2_p10,
       n7448_2_p11, n7448_2_p12, n7448_2_p13, n7448_3_p7, n7448_3_p8, n7448_3_p9, n7448_3_p10, n7448_3_p11,
       n7448_3_p12, n7448_3_p13;

  LED led_1 (.in(alu_1_p11));
  // ALU alu_1: pin names not known; wires that end beside it: A0, A1, A2, A3, B0, B1, B2, B3, S0, S1, alu_1_p11, alu_1_p12, alu_1_p13, alu_1_p14, alu_1_p15, alu_1_p16, alu_1_p17
  LED led_2 (.in(alu_1_p12));
  BinaryToBcdICs_main main_1 (
    .A0(alu_1_p14), .A1(alu_1_p15), .A2(alu_1_p16), .A3(alu_1_p17), .T0(main_1_t0), .U3(main_1_u3),
    .U2(main_1_u2), .U1(main_1_u1), .U0(main_1_u0));
  LED led_3 (.in(alu_1_p13));
  // _7448 7448_1: pin names not known; wires that end beside it: 1'b0, 1'b0, 1'b1, 1'b1, alu_1_p13, 1'b0, n7448_1_p7
  // _7448 7448_2: pin names not known; wires that end beside it: 1'b0, 1'b0, 1'b1, 1'b1, 1'b0, main_1_t0, n7448_2_p7, n7448_2_p8, n7448_2_p9, n7448_2_p10, n7448_2_p11, n7448_2_p12, n7448_2_p13
  // _7448 7448_3: pin names not known; wires that end beside it: main_1_u1, main_1_u2, 1'b1, 1'b1, main_1_u3, main_1_u0, n7448_3_p7, n7448_3_p8, n7448_3_p9, n7448_3_p10, n7448_3_p11, n7448_3_p12, n7448_3_p13
  _7_Segment_Display u_7_segment_display_1 (.g(n7448_1_p7));  // open: f, a, b, e, d, c, dp
  _7_Segment_Display u_7_segment_display_2 (
    .g(n7448_2_p8), .f(n7448_2_p7), .a(n7448_2_p9), .b(n7448_2_p10), .e(n7448_2_p13), .d(n7448_2_p12),
    .c(n7448_2_p11));  // open: dp
  _7_Segment_Display u_7_segment_display_3 (
    .g(n7448_3_p8), .f(n7448_3_p7), .a(n7448_3_p9), .b(n7448_3_p10), .e(n7448_3_p13), .d(n7448_3_p12),
    .c(n7448_3_p11));  // open: dp

  // Notes on the sheet:
  //   div by zero flag
  //   zero flag
  //   sign flag
endmodule
