// Logisim project 2bitComp.circ as structural Verilog: 2 circuits, main circuit 2bitComp
// 2bitCompar
module _2bitComp (
  input  B,
  input  A,
  output A_B,
  output A_B_2,
  output A_B_3
);

  wire n7404_1_p2, n7404_1_p6, n7486_1_p3;

  // _7486 7486_1: pin names not known; wires that end beside it: B, A, n7486_1_p3
  // _7404 7404_1: pin names not known; wires that end beside it: B, n7404_1_p2, n7486_1_p3, A_B, A, n7404_1_p6
  // _7408 7408_1: pin names not known; wires that end beside it: A, n7404_1_p2, A_B_3, n7404_1_p6, B, A_B_2
endmodule

// A>B
module _3bitComp (
  input  A2,
  input  B2,
  input  A1,
  input  B1,
  input  B0,
  input  A0,
  output A_B
);

  wire n7404_1_p2, n7404_1_p4, n7404_2_p1, n7408_1_p4, n7408_1_p6, n7408_2_p4, n7408_2_p7, n7408_2_p9,
       n7432_1_p1, n7432_1_p2, n7432_1_p3, n7432_1_p5, n7486_1_p3;

  // _7404 7404_1: pin names not known; wires that end beside it: B1, n7404_1_p2, B2, n7404_1_p4
  // _7432 7432_1: pin names not known; wires that end beside it: n7432_1_p1, n7432_1_p2, n7432_1_p3, n7432_1_p3, n7432_1_p5, A_B
  // _7408 7408_1: pin names not known; wires that end beside it: A2, n7404_1_p4, n7432_1_p1, n7408_1_p4, A1, n7408_1_p6
  // _7408 7408_2: pin names not known; wires that end beside it: n7408_1_p6, n7404_1_p2, n7432_1_p2, n7408_2_p4, B0, n7432_1_p5, n7408_2_p7, n7408_1_p4, n7408_2_p9, n7408_2_p9, A0, n7408_2_p4, n7408_2_p7
  // _7486 7486_1: pin names not known; wires that end beside it: B2, A2, n7486_1_p3, A1, B1
  // _7404 7404_2: pin names not known; wires that end beside it: n7404_2_p1, n7486_1_p3, n7408_1_p4, n7404_2_p1
endmodule
