// Logisim project AdditionCirc.circ as structural Verilog: 1 circuit, main circuit main
// Add
module main (
  input  A0,
  input  A3,
  input  A1,
  input  B3,
  input  A2,
  input  B0,
  input  B1,
  input  B2,
  output TSum0,
  output TSum1,
  output TSum2,
  output TSum3,
  output SumSign
);

  wire addition_subtraction_1_sub0, addition_subtraction_1_sub1, addition_subtraction_1_sub2,
       addition_subtraction_1_sub3, addition_subtraction_1_sum0, addition_subtraction_1_sum1,
       addition_subtraction_1_sum2, addition_subtraction_1_sum3, n3bitcomp_1_a_b, n7404_1_p2, n7408_1_p3,
       n7408_1_p6, n7486_1_p3;

  _2Bit_Mult u_2bit_mult_1 (
    .I1(addition_subtraction_1_sum0), .Base(n7486_1_p3), .I0(addition_subtraction_1_sub0), .OutPut(TSum0));
  Addition_Subtraction addition_subtraction_1 (
    .A0(A0), .A1(A1), .Sum2(addition_subtraction_1_sum2), .A2(A2), .B0(B0), .B1(B1), .B2(B2), .Control(1'b1),
    .Sum1(addition_subtraction_1_sum1), .Sum0(addition_subtraction_1_sum0),
    .Sum3(addition_subtraction_1_sum3), .Sub2(addition_subtraction_1_sub2),
    .Sub1(addition_subtraction_1_sub1), .Sub0(addition_subtraction_1_sub0), .Sub3(addition_subtraction_1_sub3));
  _2Bit_Mult u_2bit_mult_2 (
    .I1(addition_subtraction_1_sum1), .Base(n7486_1_p3), .I0(addition_subtraction_1_sub1), .OutPut(TSum1));
  _2Bit_Mult u_2bit_mult_3 (
    .I1(addition_subtraction_1_sum2), .Base(n7486_1_p3), .I0(addition_subtraction_1_sub2), .OutPut(TSum2));
  _2Bit_Mult u_2bit_mult_4 (
    .I1(addition_subtraction_1_sum3), .Base(n7486_1_p3), .I0(addition_subtraction_1_sub3), .OutPut(TSum3));
  _3bitComp u_3bitcomp_1 (.B1(B1), .B0(B0), .B2(B2), .A2(A2), .A1(A1), .A0(A0), .A_B(n3bitcomp_1_a_b));
  // _7404 7404_1: pin names not known; wires that end beside it: n3bitcomp_1_a_b, n7404_1_p2
  // _7486 7486_1: pin names not known; wires that end beside it: B3, A3, n7486_1_p3
  // _7408 7408_1: pin names not known; wires that end beside it: n7404_1_p2, B3, n7408_1_p3, n3bitcomp_1_a_b, A3, n7408_1_p6
  // _7432 7432_1: pin names not known; wires that end beside it: n7408_1_p3, n7408_1_p6, SumSign
endmodule
