// Logisim project Additions&subtraction.circ as structural Verilog: 1 circuit, main circuit Addition&Subtraction
// 3bitSubtraction
module Addition_Subtraction (
  input  A0,
  input  A1,
  input  A2,
  input  B0,
  input  B1,
  input  B2,
  input  Control,
  output Sum2,
  output Sum3,
  output Sum1,
  output Sum0,
  output Sub3,
  output Sub2,
  output Sub1,
  output Sub0
);

  wire n7404_1_p2, n7483_2_p2, n7483_2_p5, n7483_2_p7, n7486_1_p3, n7486_1_p6, n7486_1_p9, n7486_2_p4,
       n7486_2_p5, n7486_2_p8, n7486_2_p10, n7486_2_p13;

  // _7483 7483_1: pin names not known; wires that end beside it: 1'b0, Sum2, A2, B2, Sum1, A1, B1, 1'b0, Sum3, 1'b0, 1'b0, B0, A0, Sum0
  // _7486 7486_1: pin names not known; wires that end beside it: B2, Control, n7486_1_p3, Control, B0, n7486_1_p6, Control, B1, n7486_1_p9
  // _7483 7483_2: pin names not known; wires that end beside it: 1'b0, n7483_2_p2, A2, n7486_1_p3, n7483_2_p5, 1'b0, n7483_2_p7, Control, n7486_1_p6
  // _7486 7486_2: pin names not known; wires that end beside it: n7486_1_p9, A1, n7483_2_p5, n7486_2_p4, n7486_2_p5, n7483_2_p2, n7486_2_p4, n7486_2_p8, A0, n7486_2_p10, n7486_2_p4, n7486_2_p10, n7486_2_p13, n7486_2_p4
  // _7483 7483_3: pin names not known; wires that end beside it: 1'b0, 1'b0, Sub2, 1'b0, n7486_2_p8, Sub1, n7486_2_p5, 1'b0, 1'b0, Sub3, n7486_2_p4, n7486_2_p13, 1'b0, Sub0
  // _7404 7404_1: pin names not known; wires that end beside it: n7483_2_p7, n7404_1_p2
  // _7408 7408_1: pin names not known; wires that end beside it: n7404_1_p2, Control, n7486_2_p4
endmodule
