// Logisim project BcdToSevenSegmentDecoder.circ as structural Verilog: 2 circuits, main circuit BcdToSevenSegmentDecoder
module BcdToSevenSegmentDecoder (
  input  A,
  input  B,
  input  C,
  input  D,
  output a_2,
  output b_2,
  output c_2,
  output d_2,
  output e,
  output f,
  output g
);

  wire B_prime, B_XOR_C, n7404_1_p4, n7404_1_p6, n7408_1_p6, n7408_1_p9, n7408_1_p12, n7408_2_p1,
       n7408_2_p10, n7408_2_p11, n7432_1_p3, n7432_1_p6, n7432_1_p7, n7432_1_p8, n7432_1_p9, n7432_2_p1,
       n7432_2_p5, n7432_3_p3, n7432_4_p9, n7486_1_p3;

  // _7404 7404_1: pin names not known; wires that end beside it: B, B_prime, C, n7404_1_p4, D, n7404_1_p6
  // _7432 7432_1: pin names not known; wires that end beside it: n7404_1_p4, n7404_1_p6, n7432_1_p3, A, C, n7432_1_p6, n7432_1_p7, n7432_1_p8, n7432_1_p9, n7432_1_p9, A, f
  // _7408 7408_1: pin names not known; wires that end beside it: B, C, D, D, B, n7408_1_p6, n7408_1_p6, n7404_1_p4, n7408_1_p9, n7404_1_p6, C, n7408_1_p12
  // _7486 7486_1: pin names not known; wires that end beside it: B_prime, D, n7486_1_p3, D, n7404_1_p4, B, C, B_XOR_C
  // _7408 7408_2: pin names not known; wires that end beside it: n7408_2_p1, n7404_1_p4, n7404_1_p6, n7432_1_p8, n7432_1_p3, B, n7432_1_p7, B_prime, C, n7408_2_p10, n7408_2_p11, n7404_1_p6, e
  // _7432 7432_2: pin names not known; wires that end beside it: n7432_2_p1, n7408_1_p9, d_2, n7408_2_p10, n7432_2_p5, n7432_2_p1, C, B_prime, n7408_2_p11, e, A, n7432_2_p5
  // _7432 7432_3: pin names not known; wires that end beside it: B_XOR_C, A, n7432_3_p3, n7432_3_p3, n7408_1_p12, g
  // _7432 7432_4: pin names not known; wires that end beside it: n7486_1_p3, n7432_1_p6, a_2, B_prime, n7408_2_p1, b_2, B, D, n7432_4_p9, n7432_4_p9, n7404_1_p4, c_2

  // Notes on the sheet:
  //   e
endmodule

module SevenSegmentDisplay (
  input  Ro_Sign_bit,
  input  T0,
  input  U3,
  input  U2,
  input  U1,
  input  U0
);

  wire bcdtosevensegmentdecoder_1_a_2, bcdtosevensegmentdecoder_1_b_2, bcdtosevensegmentdecoder_1_c_2,
       bcdtosevensegmentdecoder_1_d_2, bcdtosevensegmentdecoder_1_e, bcdtosevensegmentdecoder_1_f,
       bcdtosevensegmentdecoder_1_g;

  BcdToSevenSegmentDecoder bcdtosevensegmentdecoder_1 (
    .A(U3), .B(U2), .C(U1), .D(U0), .a_2(bcdtosevensegmentdecoder_1_a_2),
    .b_2(bcdtosevensegmentdecoder_1_b_2), .c_2(bcdtosevensegmentdecoder_1_c_2),
    .d_2(bcdtosevensegmentdecoder_1_d_2), .e(bcdtosevensegmentdecoder_1_e), .f(bcdtosevensegmentdecoder_1_f),
    .g(bcdtosevensegmentdecoder_1_g));
  _7_Segment_Display u_7_segment_display_1 (.g(Ro_Sign_bit));  // open: f, a, b, e, d, c, dp
  _7_Segment_Display u_7_segment_display_2 (.b(T0), .c(T0));  // open: g, f, a, e, d, dp
  _7_Segment_Display u_7_segment_display_3 (
    .g(bcdtosevensegmentdecoder_1_g), .f(bcdtosevensegmentdecoder_1_f), .a(bcdtosevensegmentdecoder_1_a_2),
    .b(bcdtosevensegmentdecoder_1_b_2), .e(bcdtosevensegmentdecoder_1_e), .d(bcdtosevensegmentdecoder_1_d_2),
    .c(bcdtosevensegmentdecoder_1_c_2));  // open: dp
endmodule
