// Logisim project BinaryToBcdICs.circ as structural Verilog: 1 circuit, main circuit main
module main (
  input  A0,
  input  A1,
  input  A2,
  input  A3,
  output T0,
  output U3,
  output U2,
  output U1,
  output U0
);

  wire n7404_1_p2, n7404_1_p4, n7408_1_p1, n7408_1_p4, n7408_1_p9, n7408_1_p12, n7408_2_p4, n7408_2_p7,
       n7408_2_p10;

  // _7404 7404_1: pin names not known; wires that end beside it: A1, n7404_1_p2, A2, n7404_1_p4, A3
  // _7408 7408_1: pin names not known; wires that end beside it: n7408_1_p1, n7404_1_p2, n7404_1_p4, n7408_1_p4, n7408_1_p4, A3, U3, A3, n7408_1_p9, T0, A2, n7408_1_p12, U2
  // _7408 7408_2: pin names not known; wires that end beside it: A0, A1, n7408_1_p1, n7408_2_p4, n7404_1_p2, A3, n7408_2_p7, A2, n7408_2_p7, n7408_2_p10
  // _7432 7432_1: pin names not known; wires that end beside it: n7408_1_p1, A1, n7408_1_p12, A1, A2, n7408_1_p9, n7408_2_p10, n7408_2_p4, U1

  assign U0 = A0;
endmodule
