// Logisim project FullSub.circ as structural Verilog: 3 circuits, main circuit HalfSub
// Half-
module HalfSub (
  input  A,
  input  B,
  output Sum,
  output Co
);

  wire n7404_1_p2;

  // _7486 7486_1: pin names not known; wires that end beside it: B, A, Sum
  // _7404 7404_1: pin names not known; wires that end beside it: A, n7404_1_p2
  // _7408 7408_1: pin names not known; wires that end beside it: n7404_1_p2, B, Co
endmodule

module FullSub (
  input  A,
  input  B,
  input  C,
  output Sum,
  output Co
);

  wire halfsub_1_co, halfsub_1_sum, halfsub_2_co;

  HalfSub halfsub_1 (.A(A), .B(B), .Sum(halfsub_1_sum), .Co(halfsub_1_co));
  HalfSub halfsub_2 (.A(halfsub_1_sum), .B(C), .Sum(Sum), .Co(halfsub_2_co));
  // _7432 7432_1: pin names not known; wires that end beside it: halfsub_1_co, halfsub_2_co, Co, Sum
endmodule

module _4bitSub (
  input  A0,
  input  B0,
  input  A1,
  input  B1,
  input  A2,
  input  B2,
  input  A3,
  input  B3,
  output x0,
  output x1,
  output x2,
  output x3,
  output x4
);

  wire fullsub_1_co, fullsub_2_co, halfsub_1_co;

  HalfSub halfsub_1 (.A(A0), .B(B0), .Sum(x0), .Co(halfsub_1_co));
  FullSub fullsub_1 (.A(A1), .B(B1), .C(halfsub_1_co), .Co(fullsub_1_co), .Sum(x1));
  FullSub fullsub_2 (.A(A2), .B(B2), .C(fullsub_1_co), .Co(fullsub_2_co), .Sum(x2));
  FullSub fullsub_3 (.A(A3), .B(B3), .C(fullsub_2_co), .Co(x4), .Sum(x3));
endmodule
