// Logisim project HalfAdder.circ as structural Verilog: 3 circuits, main circuit main
module main (
  input  A,
  input  B,
  output Sum,
  output Co
);

  // _7486 7486_1: pin names not known; wires that end beside it: Sum, B, A, Sum
  // _7408 7408_1: pin names not known; wires that end beside it: A, B, Co, Co
endmodule

module FullAdder (
  input  A,
  input  B,
  input  CarryIn,
  output Carryout,
  output Sum
);

  wire main_1_co, main_1_sum, n7432_1_p1;

  main main_1 (.A(A), .B(B), .Sum(main_1_sum), .Co(main_1_co));
  // _7432 7432_1: pin names not known; wires that end beside it: n7432_1_p1, main_1_co, Carryout
  main main_2 (.A(CarryIn), .B(main_1_sum), .Sum(Sum), .Co(n7432_1_p1));
endmodule

module _4_binarryAdder (
  input  in_1,
  input  in_2,
  input  in_3,
  input  in_4,
  input  in_5,
  input  in_6,
  input  in_7,
  input  in_8,
  output out_9,
  output out_10,
  output out_11,
  output out_12,
  output out_13
);

  wire fulladder_2_carryout, fulladder_3_carryout, main_1_co;

  FullAdder fulladder_1 (.A(in_1), .B(in_5), .CarryIn(fulladder_2_carryout), .Carryout(out_12), .Sum(out_10));
  FullAdder fulladder_2 (
    .A(in_2), .B(in_6), .CarryIn(fulladder_3_carryout), .Carryout(fulladder_2_carryout), .Sum(out_13));
  FullAdder fulladder_3 (.A(in_3), .B(in_7), .CarryIn(main_1_co), .Carryout(fulladder_3_carryout), .Sum(out_11));
  main main_1 (.A(in_4), .B(in_8), .Sum(out_9), .Co(main_1_co));
endmodule
