// Logisim project Main.circ as structural Verilog: 2 circuits, main circuit main
module main (
);

  ALU alu_1 ();  // open: A0, A1, A2, Div_by_zero_flag, A3_sign, B0, B1, B2, B3_sign, S0, S1, Sign_of_Rf0, Rf1, Rf3, Rf2, Zero_flag
endmodule

module ALU (
  input  A0,
  input  A1,
  input  A2,
  input  A3_sign,
  input  B0,
  input  B1,
  input  B2,
  input  B3_sign,
  input  S0,
  input  S1,
  output Sign_of_Rf0,
  output Div_by_zero_flag,
  output Rf1,
  output Rf2,
  output Zero_flag,
  output Rf3
);

  wire AD0_sign, AD1, AD2, AD3, AD4, And_p3, And_p9, DIV_BY_ZERO_FLAG_t, R0_sign, R1, R2, R3, Rf0, Sub0_sign,
       Sub1, Sub2, Sub3, Sub4;

  // Implementation_Remender implementation_remender_1: pin names not known; wires that end beside it: A3_sign, A2, A1, A0, B2, B1, B0, R0_sign, R1, R2, R3, DIV_BY_ZERO_FLAG_t
  AdditionCirc_main main_1 (
    .A0(A0), .A1(A1), .A2(A2), .B0(B0), .B1(B1), .B2(B2), .A3(A3_sign), .B3(B3_sign), .TSum0(AD1),
    .TSum1(AD2), .TSum2(AD3), .TSum3(AD4), .SumSign(AD0_sign));
  // Subtraction subtraction_1: pin names not known; wires that end beside it: A0, A1, A2, B0, B1, B2, Sub1, B3_sign, Sub2, A3_sign, Sub3, Sub4, Sub0_sign
  // _7408 And: pin names not known; wires that end beside it: S0, S1, And_p3, And_p3, DIV_BY_ZERO_FLAG_t, Div_by_zero_flag, 1'b0, 1'b1, And_p9, Rf0, Sign_of_Rf0
  // _7404 7404_1: pin names not known; wires that end beside it: Zero_flag, And_p9
  // _74253 74253_1: pin names not known; wires that end beside it: 1'b0, S1, R1, 1'b0, Sub1, AD1, Rf1, 1'b0, 1'b1, 1'b0, S0, R2, 1'b0, Sub2, AD2, Rf2
  // _74253 74253_2: pin names not known; wires that end beside it: 1'b0, S1, R3, 1'b0, Sub3, AD3, Rf3, 1'b0, 1'b1, 1'b0, S0, R0_sign, 1'b0, Sub0_sign, AD0_sign, Rf0
  // comparator_main main_2: pin names not known; wires that end beside it: Rf1, Rf2, Rf3, 1'b0, 1'b0, 1'b0, 1'b0, 1'b0, 1'b1, 1'b1, 1'b1, Zero_flag

  // Notes on the sheet:
  //   just connect inputs to add and subtraction
  //   Add
  //   subtraction
  //   should ouput one only if selector 11
  //   our group is only 3 so there is no 10 multipllication as selection its forbiden so we will leave it empty or ground
  //   note you can not have -zero so we should AND it with not zeroflag
  //   Righ side of mux for sign
endmodule
