// Logisim project Mux.circ as structural Verilog
module _2Bit_Mult (
  input  I0,
  input  Base,
  input  I1,
  output OutPut
);

  wire n7400_1_p1, n7400_1_p3, n7400_1_p4;

  // _7400 7400_1: pin names not known; wires that end beside it: n7400_1_p1, I1, n7400_1_p3, n7400_1_p4, n7400_1_p3, OutPut
  // _7400 7400_2: pin names not known; wires that end beside it: OutPut, I0, Base, n7400_1_p4, Base, Base, n7400_1_p1
endmodule
