// Logisim project Remainder Bassem.circ as structural Verilog: 3 circuits, main circuit Remaind to Test 
module Remaind_to_Test (
  input  in_1,
  input  in_2,
  input  in_3,
  input  in_4,
  input  in_5,
  input  in_6,
  input  in_7,
  output Sign_of_result,
  output R0,
  output R1,
  output R2,
  output Div_by_zero_flag,
  output Zero_flag
);

  Implementation_Remender implementation_remender_1 (
    .Sign_of_A(in_1), .Sign_of_result(Sign_of_result), .Rfinal0(R0), .Rfinal1(R1), .Zero_flag(Zero_flag),
    .Rfinal2(R2), .DIV_by_zero_flag(Div_by_zero_flag), .A2(in_2), .A1(in_3), .A0(in_4), .B2(in_5), .B1(in_6),
    .B0(in_7));

  // Other names for the same wires on the sheet: A0 = in_4; A1 = in_3; A2 = in_2; B0 = in_7; B1 = in_6; B2 = in_5;
  //   Sign_of_A = in_1

  // Notes on the sheet:
  //   note assume zero flag is not implemented here its only to test but i will do it in alu better
endmodule

module Implementation_Remender (
  input  A2,
  input  A1,
  input  A0,
  input  B2,
  input  B1,
  input  B0,
  input  Sign_of_A,
  output Rfinal0,
  output Rfinal1,
  output Rfinal2,
  output Sign_of_result,
  output DIV_by_zero_flag,
  output Zero_flag
);

  wire A__2B, A__B, main_1_yeq, main_1_ygt, main_2_yeq, main_3_yeq, MUX2X1_p4, MUX2X1_p7, MUX2X1_p13,
       n7408_2_p1, Not_p2, OR_2_p3, R0, R1, R2, s0, s1, Xor_p6, y0, y1, y2;

  comparator_main main_1 (
    .A1(A0), .A2(A1), .A3(A2), .A4(1'b0), .B1(B0), .B2(B1), .B3(B2), .B4(1'b0), .CLT(1'b1), .CEQ(1'b1),
    .CGT(1'b1), .YEQ(main_1_yeq), .YGT(main_1_ygt));  // open: YLT
  comparator_main main_2 (
    .A1(B0), .A2(B1), .A3(B2), .A4(1'b0), .B1(1'b0), .B2(1'b1), .B3(1'b0), .B4(1'b0), .CLT(1'b1), .CEQ(1'b1),
    .CGT(1'b1), .YEQ(main_2_yeq));  // open: YLT, YGT
  comparator_main main_3 (
    .A1(B0), .A2(B1), .A3(B2), .A4(1'b0), .B1(1'b1), .B2(1'b0), .B3(1'b0), .B4(1'b0), .CLT(1'b1), .CEQ(1'b1),
    .CGT(1'b1), .YEQ(main_3_yeq));  // open: YLT, YGT
  comparator_main main_4 (
    .A1(B0), .A2(B1), .A3(B2), .A4(1'b0), .B1(1'b0), .B2(1'b0), .B3(1'b0), .B4(1'b0), .CLT(1'b1), .CEQ(1'b1),
    .CGT(1'b1), .YEQ(DIV_by_zero_flag));  // open: YLT, YGT
  _4_bit_comparartor _4_bit_Comparator (
    .A0(A0), .B0(1'b0), .A1(A1), .B1(B0), .A2(A2), .B2(B1), .A3(1'b0), .B3(B2), .A____B(A__2B));  // open: A_B
  // _7432 OR: pin names not known; wires that end beside it: main_1_yeq, main_1_ygt, A__B, 1'b0, 1'b1
  // _7404 Not: pin names not known; wires that end beside it: 1'b1, Not_p2, s0
  // _7486 Xor: pin names not known; wires that end beside it: main_2_yeq, DIV_by_zero_flag, Not_p2, main_3_yeq, DIV_by_zero_flag, Xor_p6, 1'b0, 1'b1, Xor_p6, s1, 1'b0
  // _74157 MUX2X1: pin names not known; wires that end beside it: A__2B, B0, 1'b0, MUX2X1_p4, B1, B0, MUX2X1_p7, 1'b0, 1'b1, 1'b0, B2, B1, MUX2X1_p13
  // _7408 7408_1: pin names not known; wires that end beside it: MUX2X1_p4, A__B, y0, MUX2X1_p7, A__B, y1, 1'b0, 1'b1, MUX2X1_p13, A__B, y2
  // _74253 MUX4X2: pin names not known; wires that end beside it: A2, 1'b0, s1, R2, 1'b0, 1'b0, 1'b0, Rfinal2, 1'b0, 1'b0, 1'b0, s0, s0
  // _74253 MUX4X2_2: pin names not known; wires that end beside it: 1'b0, s1, R0, A0, 1'b0, 1'b0, Rfinal0, 1'b0, s0, R1, 1'b0, 1'b0, 1'b0, Rfinal1, A1
  // _7408 7408_2: pin names not known; wires that end beside it: n7408_2_p1, Sign_of_A, Sign_of_result, 1'b0, 1'b1
  // _7432 OR_2: pin names not known; wires that end beside it: Rfinal0, Rfinal1, OR_2_p3, OR_2_p3, Rfinal2, n7408_2_p1, 1'b0, 1'b1, 1'b0
  comparator_main main_5 (
    .A1(Rfinal0), .A2(Rfinal1), .A3(Rfinal2), .A4(1'b0), .B1(1'b0), .B2(1'b0), .B3(1'b0), .B4(1'b0),
    .CLT(1'b1), .CEQ(1'b1), .CGT(1'b1), .YEQ(Zero_flag));  // open: YLT, YGT
  _4bitSub Full_subtractor (.A0(A0), .B0(y0), .A1(A1), .B1(y1), .A2(A2), .B2(y2), .x0(R0), .x1(R1), .x2(R2));

  // Notes on the sheet:
  //   if B==1
  //   if B==0
  //   if B==2
  //   note there is no ic comparator so i created a one
  //   If N1>=<N2 except for N2= 0,1,2
  //   IF N2==2,1,0 
  //   0
  //   1
  //   note assume zero flag is not implemented here its only to test but i will do it in alu instead
  //   note mux is active low
endmodule

module _4_bit_comparartor (
  input  A0,
  input  B0,
  input  A1,
  input  B1,
  input  A2,
  input  B2,
  input  A3,
  input  B3,
  output A____B,
  output A_B
);

  wire and_1_out, and_2_out, and_3_out, and_4_out, and_5_out, and_6_out, and_7_out, and_8_out, and_9_out,
       and_10_out, not_1_out, not_2_out, not_3_out, not_4_out, or_1_out, or_2_out, xnor_1_out, xnor_2_out,
       xnor_3_out;

  not not_1 (not_1_out, A0);
  not not_2 (not_2_out, A1);
  not not_3 (not_3_out, A2);
  not not_4 (not_4_out, A3);
  and and_1 (and_1_out, not_1_out, B0);
  xnor xnor_1 (xnor_1_out, A1, B1);
  and and_2 (and_2_out, not_2_out, B1);
  xnor xnor_2 (xnor_2_out, A2, B2);
  and and_3 (and_3_out, not_3_out, B2);
  xnor xnor_3 (xnor_3_out, A3, B3);
  and and_4 (and_4_out, not_4_out, B3);
  and and_5 (and_5_out, and_1_out, xnor_1_out);
  and and_6 (and_6_out, xnor_2_out, xnor_3_out);
  and and_7 (and_7_out, and_2_out, xnor_2_out);
  and and_8 (and_8_out, and_3_out, xnor_3_out);
  and and_9 (and_9_out, and_5_out, and_6_out);
  and and_10 (and_10_out, and_7_out, xnor_3_out);
  or or_1 (or_1_out, and_9_out, and_10_out);
  or or_2 (or_2_out, and_8_out, and_4_out);
  or or_3 (A_B, or_1_out, or_2_out);
  not not_5 (A____B, A_B);
endmodule
