// Logisim project SubtractionCirc.circ as structural Verilog: 1 circuit, main circuit Subtraction
// Sub
module Subtraction (
  input  A0,
  input  A1,
  input  A2,
  input  B3,
  input  A3,
  input  B0,
  input  B1,
  input  B2,
  output TSub1,
  output TSub3,
  output TSub0,
  output TSub2,
  output SubSign
);

  wire addition_subtraction_1_sub0, addition_subtraction_1_sub1, addition_subtraction_1_sub2,
       addition_subtraction_1_sub3, addition_subtraction_1_sum0, addition_subtraction_1_sum1,
       addition_subtraction_1_sum2, addition_subtraction_1_sum3, n3bitcomp_1_a_b, n7404_1_p2, n7486_1_p3;

  _2Bit_Mult u_2bit_mult_1 (
    .I1(addition_subtraction_1_sub0), .Base(n7486_1_p3), .I0(addition_subtraction_1_sum0), .OutPut(TSub0));
  Addition_Subtraction addition_subtraction_1 (
    .A0(A0), .A1(A1), .Sum2(addition_subtraction_1_sum2), .A2(A2), .B0(B0), .B1(B1), .B2(B2), .Control(1'b1),
    .Sum1(addition_subtraction_1_sum1), .Sum0(addition_subtraction_1_sum0),
    .Sum3(addition_subtraction_1_sum3), .Sub2(addition_subtraction_1_sub2),
    .Sub1(addition_subtraction_1_sub1), .Sub0(addition_subtraction_1_sub0), .Sub3(addition_subtraction_1_sub3));
  _2Bit_Mult u_2bit_mult_2 (
    .I1(addition_subtraction_1_sub1), .Base(n7486_1_p3), .I0(addition_subtraction_1_sum1), .OutPut(TSub1));
  _2Bit_Mult u_2bit_mult_3 (
    .I1(addition_subtraction_1_sub2), .Base(n7486_1_p3), .I0(addition_subtraction_1_sum2), .OutPut(TSub2));
  _2Bit_Mult u_2bit_mult_4 (
    .I1(addition_subtraction_1_sub3), .Base(n7486_1_p3), .I0(addition_subtraction_1_sum3), .OutPut(TSub3));
  _3bitComp u_3bitcomp_1 (.B1(B1), .B0(B0), .B2(B2), .A2(A2), .A1(A1), .A0(A0), .A_B(n3bitcomp_1_a_b));
  // _7404 7404_1: pin names not known; wires that end beside it: n3bitcomp_1_a_b, n7404_1_p2
  // _7486 7486_1: pin names not known; wires that end beside it: A3, B3, n7486_1_p3
  _2Bit_Mult u_2bit_mult_5 (.I1(n7404_1_p2), .Base(A3), .I0(n3bitcomp_1_a_b), .OutPut(SubSign));
endmodule
